// Logisim project UAL.circ as structural Verilog
module half_add (
  input  A,
  input  B,
  output out_3,
  output out_4
);

  xor xor_1 (out_3, A, B);
  and and_1 (out_4, B, A);
endmodule

module add (
  input  A,
  input  B,
  input  R,
  output S,
  output R_2
);

  wire half_add_1_out_3, half_add_1_out_4, half_add_2_out_4;

  half_add half_add_1 (.A(B), .B(R), .out_3(half_add_1_out_3), .out_4(half_add_1_out_4));
  half_add half_add_2 (.A(A), .B(half_add_1_out_3), .out_3(S), .out_4(half_add_2_out_4));
  or or_1 (R_2, half_add_2_out_4, half_add_1_out_4);
endmodule

// ADD
module add_4_bits (
  input  A0,
  input  A1,
  input  B0,
  input  B1,
  output out_5,
  output out_6,
  output out_7,
  output out_8
);

  wire half_add_1_out_4;

  half_add half_add_1 (.A(A0), .B(B0), .out_3(out_5), .out_4(half_add_1_out_4));
  add add_1 (.A(half_add_1_out_4), .B(A1), .R(B1), .S(out_6), .R_2(out_7));

  assign out_8 = 1'b0;
endmodule

// INVER
module inverseur (
  input  D0,
  input  D1,
  input  D2,
  input  D3,
  output out_5,
  output out_6,
  output out_7,
  output out_8
);

  not not_1 (out_5, D0);
  not not_2 (out_6, D1);
  not not_3 (out_7, D2);
  not not_4 (out_8, D3);
endmodule

module OR (
  input  A0,
  input  A1,
  input  B0,
  input  B1,
  output out_5,
  output out_6,
  output out_7,
  output out_8
);

  or or_1 (out_5, A0, A1);
  or or_2 (out_6, B0, B1);

  assign out_7 = 1'b0;
  assign out_8 = 1'b0;
endmodule

// COMP
module comparateur (
  input  D0,
  input  D1,
  input  D2,
  input  D3,
  output out_5,
  output out_6,
  output out_7,
  output out_8
);

  or or_1 (out_5, D0, D1, D2, D3);

  assign out_6 = 1'b0;
  assign out_7 = 1'b0;
  assign out_8 = 1'b0;
endmodule

module multiplexeur (
  input  A1,
  input  A0,
  input  D0,
  input  D1,
  input  D2,
  input  D3,
  output out_7
);

  wire and_1_out, and_2_out, and_3_out, and_4_out, not_1_out, not_2_out;

  not not_1 (not_1_out, A1);
  not not_2 (not_2_out, A0);
  and and_1 (and_1_out, not_2_out, not_1_out, D0);
  and and_2 (and_2_out, A0, not_1_out, D1);
  and and_3 (and_3_out, not_2_out, A1, D2);
  and and_4 (and_4_out, A0, A1, D3);
  or or_1 (out_7, and_1_out, and_2_out, and_3_out, and_4_out);
endmodule

module UAL (
  input  A1,
  input  A0,
  input  D3,
  input  D2,
  input  D1,
  input  D0,
  output R0,
  output R1,
  output R2,
  output R3
);

  wire add_4_bits_1_out_5, add_4_bits_1_out_6, add_4_bits_1_out_7, add_4_bits_1_out_8, comparateur_1_out_5,
       comparateur_1_out_6, comparateur_1_out_7, comparateur_1_out_8, inverseur_1_out_5, inverseur_1_out_6,
       inverseur_1_out_7, inverseur_1_out_8, or_1_out_5, or_1_out_6, or_1_out_7, or_1_out_8;

  add_4_bits add_4_bits_1 (
    .A0(D0), .A1(D1), .B0(D2), .B1(D3), .out_5(add_4_bits_1_out_5), .out_6(add_4_bits_1_out_6),
    .out_7(add_4_bits_1_out_7), .out_8(add_4_bits_1_out_8));
  inverseur inverseur_1 (
    .D0(D0), .D1(D1), .D2(D2), .D3(D3), .out_5(inverseur_1_out_5), .out_6(inverseur_1_out_6),
    .out_7(inverseur_1_out_7), .out_8(inverseur_1_out_8));
  comparateur comparateur_1 (
    .D0(D0), .D1(D1), .D2(D2), .D3(D3), .out_5(comparateur_1_out_5), .out_6(comparateur_1_out_6),
    .out_7(comparateur_1_out_7), .out_8(comparateur_1_out_8));
  OR or_1 (
    .A0(D0), .A1(D1), .B0(D2), .B1(D3), .out_5(or_1_out_5), .out_6(or_1_out_6), .out_7(or_1_out_7),
    .out_8(or_1_out_8));
  multiplexeur multiplexeur_1 (
    .D0(add_4_bits_1_out_5), .D1(inverseur_1_out_5), .D2(comparateur_1_out_5), .D3(or_1_out_5), .A1(A1),
    .A0(A0), .out_7(R0));
  multiplexeur multiplexeur_2 (
    .D0(add_4_bits_1_out_6), .D1(inverseur_1_out_6), .D2(comparateur_1_out_6), .D3(or_1_out_6), .A1(A1),
    .A0(A0), .out_7(R1));
  multiplexeur multiplexeur_3 (
    .D0(add_4_bits_1_out_7), .D1(inverseur_1_out_7), .D2(comparateur_1_out_7), .D3(or_1_out_7), .A1(A1),
    .A0(A0), .out_7(R2));
  multiplexeur multiplexeur_4 (
    .D0(add_4_bits_1_out_8), .D1(inverseur_1_out_8), .D2(comparateur_1_out_8), .D3(or_1_out_8), .A1(A1),
    .A0(A0), .out_7(R3));
endmodule
